# Fritzing sketch PowerCtrl (saved by Fritzing 0.9.2b)
breadboards: 1

parts:
  U1 = attiny85 [package=dip]
  R2 = Resistor [tolerance=±5% resistance=10k package=THT]
  R1 = PHOTOCELL [package=photocell]
  R3 = Trimmer Potentiometer [maximum_resistance=10kΩ package=THT]
  R4 = Trimmer Potentiometer [maximum_resistance=10kΩ package=THT]
  R5 = Resistor [tolerance=±5% resistance=1k package=THT]
  C1 = Electrolytic Capacitor [capacitance=10µF package="100 mil [THT, electrolytic]"]
  S1 = Pushbutton [package=THT]

nets:
  N1: U1.Pin_2, R2.Pin_0, R1.P$2, S1.leg1
  N2: U1.Pin_3, R3.wiper
  GND: U1.Pin_4, R1.P$1, R3.leg1, R5.Pin_0, C1.-, S1.leg0
  Output: U1.Pin_5
  N3: U1.Pin_7, R4.wiper
  5V: U1.Pin_8, R2.Pin_1, R3.leg2, R4.leg2, C1.+
  N4: R4.leg1, R5.Pin_1

notes:
  PowerCtrl, 1.0
